// Logisim project spm.circ as structural Verilog: 3 circuits, main circuit main
module main (
  input  in_1,
  input  in_2,
  input  in_3,
  input  in_4,
  input  in_5,
  input  in_6,
  input  BTNC
);

  wire shift_register_2_p1, shift_register_2_p9, shift_register_2_p10, shift_register_2_p11,
       shift_register_2_p12, shift_register_2_p13, shift_register_2_p14, shift_register_2_p15,
       shift_register_2_p16, undriven, undriven_2;

  // Shift_Register shift_register_1: pin names not known
  // AND_Gate and_1 is placed but not wired
  // AND_Gate and_2 has open pins: in0=BTNC, in1=shift_register_2_p16, out=open
  // AND_Gate and_3 is placed but not wired
  // AND_Gate and_4 has open pins: in0=BTNC, in1=shift_register_2_p15, out=open
  // Shift_Register shift_register_2: pin names not known; wires that end beside it: shift_register_2_p1, shift_register_2_p1, in_2, in_4, in_1, in_3, in_5, in_6, shift_register_2_p9, shift_register_2_p10, shift_register_2_p11, shift_register_2_p12, shift_register_2_p13, shift_register_2_p14, shift_register_2_p15, shift_register_2_p16
  // AND_Gate and_5 has open pins: in0=BTNC, in1=shift_register_2_p14, out=open
  // AND_Gate and_6 has open pins: in0=BTNC, in1=shift_register_2_p13, out=open
  // AND_Gate and_7 has open pins: in0=BTNC, in1=shift_register_2_p12, out=open
  // AND_Gate and_8 has open pins: in0=BTNC, in1=shift_register_2_p11, out=open
  // AND_Gate and_9 has open pins: in0=BTNC, in1=shift_register_2_p10, out=open
  // XOR_Gate xor_1 has open pins: in0=undriven, in1=undriven_2, out=open
  // AND_Gate and_10 has open pins: in0=BTNC, in1=shift_register_2_p9, out=open
  // Shift_Register #(.length(16)) shift_register_3: pin names not known; wires that end beside it: BTNC
  // AND_Gate and_11 is placed but not wired

  // Notes on the sheet:
  //   CNTRL
  //   CNTRL
  //   sign multiplicand 
  //   sign multiplier
  //   CNTRL
endmodule

module TCMP (
  input  x,
  input  clk,
  input  reset,
  output S
);

  wire not_1_out;

  not not_1 (not_1_out, x);
  D_Flip_Flop d_ff_1 (.D(not_1_out), .clk(clk), .Q(S), .reset(reset));  // open: Qn, preset
endmodule

module CSAdder (
  input  A,
  input  B,
  input  Cin,
  input  clk,
  input  reset,
  output out_6,
  output Ci
);

  wire and_1_out, and_2_out, or_1_out, xor_1_out, xor_2_out;

  xor xor_1 (xor_1_out, A, B);
  and and_1 (and_1_out, A, B);
  xor xor_2 (xor_2_out, xor_1_out, Cin);
  and and_2 (and_2_out, xor_1_out, Cin);
  D_Flip_Flop d_ff_1 (.D(xor_2_out), .clk(clk), .Q(out_6), .reset(reset));  // open: Qn, preset
  or or_1 (or_1_out, and_1_out, and_2_out);
  D_Flip_Flop d_ff_2 (.D(or_1_out), .clk(clk), .Q(Ci), .reset(reset));  // open: Qn, preset

  // Notes on the sheet:
  //   S1
  //   C1
  //   Si
  //   C2
  //   Ci
endmodule
